# Fritzing sketch LED_sonar (saved by Fritzing 0.9.0b)

parts:
  LCD1 = LCD screen
  R1 = Rotary Potentiometer (Small) [maximum_resistance=100kΩ package=THT]
  U2 = HC-SR04 [chip_label=IC package="SIP (Single Inline) [THT]"]
  Part1 = Arduino Uno (Rev3)

nets:
  GND: LCD1.VSS, LCD1.LED-, R1.leg2, U2.GND, Part1.GND
  VDD: LCD1.VDD, LCD1.LED+, R1.leg1, U2.Vcc, Part1.5V
  N1: LCD1.V0, R1.wiper
  N2: LCD1.RS, Part1.D12/MISO
  N3: LCD1.R/W, Part1.D11_PWM/MOSI
  N4: LCD1.E, Part1.D10_PWM/SS
  N5: LCD1.DB0, Part1.D9_PWM
  N6: LCD1.DB1, Part1.D8
  N7: LCD1.DB2, Part1.D7
  N8: LCD1.DB3, Part1.D6_PWM
  N9: LCD1.DB4, Part1.D5_PWM
  N10: LCD1.DB5, Part1.D4
  N11: LCD1.DB6, Part1.D3_PWM
  N12: LCD1.DB7, Part1.D2
  N13: U2.Trig, U2.Echo, Part1.D13/SCK

custom parts:
  HC-SR04: HC-SR04 ultrasound distance sensor
