# Fritzing sketch Schema (saved by Fritzing 0.9.0b)
breadboards: 1

parts:
  Arduino_Uno = Arduino Uno (Rev3)
  RELAY1 = RELAY-SOLIDSTATE [package=relay-s108t02]
  RELAY3 = RELAY-SOLIDSTATE [package=relay-s108t02]
  RELAY2 = RELAY-SOLIDSTATE [package=relay-s108t02]
  RELAY4 = RELAY-SOLIDSTATE [package=relay-s108t02]
  RELAY5 = RELAY-SOLIDSTATE [package=relay-s108t02]
  R1 = Resistor [tolerance=±5% resistance=220 package=THT]
  R2 = Resistor [tolerance=±5% resistance=220 package=THT]
  R3 = Resistor [tolerance=±5% resistance=220 package=THT]
  R4 = Resistor [tolerance=±5% resistance=220 package=THT]
  R5 = Resistor [tolerance=±5% resistance=220 package=THT]
  Appliance = mystery part, 2 pins

nets:
  N1: Arduino_Uno.D9_PWM, Appliance.pin2
  N2: Arduino_Uno.GND, RELAY1.T2, RELAY3.T2, RELAY2.T2, RELAY4.T2, RELAY5.T2, Appliance.pin1
  N3: Arduino_Uno.D2, RELAY1.T1, R5.Pin_1
  N4: Arduino_Uno.D3_PWM, RELAY2.T1, R4.Pin_1
  N5: Arduino_Uno.D4, RELAY3.T1, R3.Pin_1
  N6: Arduino_Uno.D5_PWM, RELAY4.T1, R2.Pin_1
  N7: Arduino_Uno.D6_PWM, RELAY5.T1, R1.Pin_1
  N8: Arduino_Uno.5V, R1.Pin_0, R2.Pin_0, R3.Pin_0, R4.Pin_0, R5.Pin_0
  5V: RELAY1.+, RELAY3.+, RELAY2.+, RELAY4.+, RELAY5.+
  GND: RELAY1.-, RELAY3.-, RELAY2.-, RELAY4.-, RELAY5.-

notes:
  Generic outside relay config
